# Fritzing sketch Uno (saved by Fritzing 0.9.1b)
circuit board: 6.9215cm x 5.33756cm

parts:
  Motor_Encoder = screw terminal, 4 pins
  R1 = Resistor [tolerance=±5% resistance=100 package=THT]
  R2 = Resistor [tolerance=±5% resistance=100 package=THT]
  Serial = screw terminal, 2 pins
  Cikis_1 = screw terminal, 2 pins
  Cikis_2 = screw terminal, 2 pins
  Giris_1 = screw terminal, 2 pins
  Giris_2 = screw terminal, 2 pins
  Q2 = Basic FET N-Channel [package="TO220 [THT]"]
  Analog = screw terminal, 3 pins
  T1 = LM35 Temperature Sensor [package="TO92 [THT]"]
  Q1 = Basic FET N-Channel [package="TO220 [THT]"]
  Motor_PWM-DIR = screw terminal, 8 pins
  Part1 = Arduino Uno (Rev3)
  GND = screw terminal, 2 pins

nets:
  N1: Motor_Encoder.pin1, Part1.A3
  N2: Motor_Encoder.pin2, Part1.A2
  N3: Motor_Encoder.pin3, Part1.A1
  N4: Motor_Encoder.pin4, Part1.A0
  GND: R1.Pin_0, R2.Pin_0, Analog.pin2, T1.GND, Part1.GND, GND.pin1, GND.pin2
  N5: R1.Pin_1, Q1.gate, Part1.D13/SCK
  N6: R2.Pin_1, Q2.gate, Part1.D12/MISO
  N7: Serial.pin1, Part1.D11_PWM/MOSI
  N8: Serial.pin2, Part1.D10_PWM/SS
  N9: Cikis_1.pin1, Q2.drain
  N10: Cikis_1.pin2, Giris_2.pin2
  N11: Cikis_2.pin1, Q1.drain
  N12: Cikis_2.pin2, Giris_1.pin2
  N13: Giris_1.pin1, Q1.source
  N14: Giris_2.pin1, Q2.source
  N15: Analog.pin1, Part1.A4/SDA
  N16: Analog.pin3, T1.+Vs, Part1.5V
  N17: T1.Vout, Part1.A5/SCL
  N18: Motor_PWM-DIR.pin1, Part1.D9_PWM
  N19: Motor_PWM-DIR.pin2, Part1.D8
  N20: Motor_PWM-DIR.pin3, Part1.D7
  N21: Motor_PWM-DIR.pin4, Part1.D6_PWM
  N22: Motor_PWM-DIR.pin5, Part1.D5_PWM
  N23: Motor_PWM-DIR.pin6, Part1.D4
  N24: Motor_PWM-DIR.pin7, Part1.D3_PWM
  N25: Motor_PWM-DIR.pin8, Part1.D2

notes:
  Motor PWM DIR
  Serial
  Encoder
  TCRT
  LM35
  Cikis 1
  Giris 2
  GND
  Robotek Kulubu
  NO101S
