# Fritzing sketch Şarj İstasyonu Akü (saved by Fritzing 0.9.2b)
circuit board: 9.27565cm x 8.55801cm
breadboards: 3

parts:
  Güneş_Paneli = screw terminal, 2 pins
  Eleman7 = songle relay
  Q8 = NPN-Transistor [package="TO92 [THT]"]
  D8 = Rectifier Diode [part_number=1N4001 package="300 mil [THT]"]
  R15 = Resistor [tolerance=±5% resistance=220 package=THT]
  LED5 = LED - 5mm [color="Red (633nm)" package="5 mm [THT]"]
  S6 = Pushbutton [package=THT]
  XTAL2 = Crystal [frequency="16 Mhz" package=THT]
  U4 = atmega328 [package=dip]
  C7 = Capacitor [package=cap-pth-small2]
  C8 = Capacitor [package=cap-pth-small2]
  R10 = Resistor [tolerance=±5% resistance=100 package=THT]
  R16 = Resistor [tolerance=±5% resistance=220 package=THT]
  Akü_Giriş = screw terminal, 2 pins
  12V_Çıkış = screw terminal, 2 pins
  SD- = Header 1 [package=1x01_offset]
  SD+ = Header 1 [package=1x01_offset]
  5V+ = Header 1 [package=1x01_offset]
  5V- = Header 1 [package=1x01_offset]
  5V_Çıkış = screw terminal, 2 pins
  Eleman9 = songle relay
  Q10 = NPN-Transistor [package="TO92 [THT]"]
  D10 = Rectifier Diode [part_number=1N4001 package="300 mil [THT]"]
  R22 = Resistor [tolerance=±5% resistance=220 package=THT]
  LED7 = LED - 5mm [color="Red (633nm)" package="5 mm [THT]"]
  R23 = Resistor [tolerance=±5% resistance=220 package=THT]
  Akü_Şarj = screw terminal, 2 pins
  12V_Çıkış_Motor = screw terminal, 2 pins
  5V_Çıkış_Motor = screw terminal, 2 pins
  D11 = Rectifier Diode [part_number=1N4001 package="300 mil [THT]"]
  U5 = Voltage Regulator - 5V [package="TO220 [THT]"]
  C10 = Electrolytic Capacitor [capacitance=100µF package="100 mil [THT, electrolytic]"]
  C11 = Electrolytic Capacitor [capacitance=100nF package="100 mil [THT, electrolytic]"]
  R24 = Resistor [tolerance=±5% resistance=220 package=THT]
  LED8 = LED - 5mm [color="Green (555nm)" package="5 mm [THT]"]
  R25 = Resistor [tolerance=±5% resistance=220 package=THT]
  LED9 = LED - 5mm [color="Yellow (585nm)" package="5 mm [THT]"]
  R26 = Resistor [tolerance=±5% resistance=220 package=THT]
  LED10 = LED - 5mm [color="Red (633nm)" package="5 mm [THT]"]
  S7 = Toggle Switch [package=THT]

nets:
  GND: Güneş_Paneli.pin1, Q8.C, S6.leg1, U4.GND, C7.2, C8.1, Akü_Giriş.pin2, 12V_Çıkış.pin2, SD+.1, 5V-.1, 5V_Çıkış.pin2, Q10.C, Akü_Şarj.pin2, 12V_Çıkış_Motor.pin2, 5V_Çıkış_Motor.pin2, U5.GND, C10.-, C11.-, R24.Pin_1, R25.Pin_1, R26.Pin_1
  N1: Güneş_Paneli.pin2, Eleman9.CT
  N2: Eleman7.B, Akü_Şarj.pin1
  N3: Eleman7.COIL1, Eleman7.CT, D8.cathode, R15.Pin_1, Eleman9.COIL1, D10.cathode, R22.Pin_1, U5.input_voltage, C10.+, S7.COM
  N4: Eleman7.COIL2, Q8.E, D8.anode, LED5.cathode
  N5: Eleman7.A, 12V_Çıkış.pin1, SD-.1, 12V_Çıkış_Motor.pin1, D11.anode
  N6: Q8.B, R16.Pin_1
  N7: R15.Pin_0, LED5.anode
  N8: S6.leg0, U4.RESET, R10.Pin_1
  N9: XTAL2.pin_0, U4.XLAT2, C8.2
  N10: XTAL2.pin_1, U4.XLAT1, C7.1
  N11: U4.VCC, U4.AVCC, R10.Pin_0, U5.output_voltage, C11.+
  N12: U4.D7, R16.Pin_0
  N13: U4.D8, R23.Pin_0
  N14: U4.D11_(PWM), LED9.anode
  N15: U4.D12, LED8.anode
  N16: U4.D13, LED10.anode
  N17: Akü_Giriş.pin1, S7.L2
  N18: 5V+.1, 5V_Çıkış.pin1, 5V_Çıkış_Motor.pin1
  N19: Eleman9.COIL2, Q10.E, D10.anode, LED7.cathode
  N20: Eleman9.A, D11.cathode
  N21: Q10.B, R23.Pin_1
  N22: R22.Pin_0, LED7.anode
  N23: R24.Pin_0, LED8.cathode
  N24: R25.Pin_0, LED9.cathode
  N25: R26.Pin_0, LED10.cathode
